# Fritzing sketch 6502_computer (saved by Fritzing 0.9.3b)
breadboards: 6

parts:
  U1 = 74HC04_HEX_INVERTER [package=dil14]
  IC1 = 74HC08 Logic AND Gate [part_number=74HC08 package="DIP (Dual Inline) [THT]"]
  IC2 = IC, DIP package, 20 pins [chip_label=74HCT688E]
  IC3 = IC, DIP package, 20 pins [chip_label=74HCT688E]
  IC4 = IC, DIP package, 20 pins [chip_label=74HCT688E]
  IC5 = 74HC08 Logic AND Gate [part_number=74HC08 package="DIP (Dual Inline) [THT]"]  # not connected
  Q1 = NPN-Transistor [package="TO92 [THT]"]  # not connected
  U2 = 74HC04_HEX_INVERTER [package=dil14]  # not connected
  IC6 = IC, DIP package, 16 pins [chip_label=74LS161A]  # not connected
  Q2 = NPN-Transistor [package="TO92 [THT]"]  # not connected
  U3 = 74HC595 [package="DIP16 [THT]"]  # not connected
  U4 = 74HC595 [package="DIP16 [THT]"]  # not connected
  IC7 = IC, DIP package, 20 pins [chip_label=74LS244AN]  # not connected
  U5 = SWITCH_SPDT [package=kps-1290]  # not connected
  IC8 = IC, DIP package, 40 pins [chip_label="WDC 65C02"]  # not connected
  U6 = SWITCH_SPDT [package=kps-1290]  # not connected

nets:
  GND: U1.GND, IC1.GND, IC2.pin10, IC3.pin10, IC4.pin10
  VCC: U1.VCC, IC1.VCC, IC2.pin20, IC3.pin20, IC4.pin20
